# Fritzing sketch DosingPumps (saved by Fritzing 0.9.3b)
breadboards: 1

parts:
  Part3 = Adafruit Pro Trinket 3.3V 12MHz [part_number="Adafruit #2010"]
  PART5 = Big Easy Driver ROB-11876 [part_number=ROB-11876]
  PART6 = Big Easy Driver ROB-11876 [part_number=ROB-11876]
  Part2 = Adafruit Pro Trinket 3.3V 12MHz [part_number="Adafruit #2010"]
  PART3 = Big Easy Driver ROB-11876 [part_number=ROB-11876]
  PART4 = Big Easy Driver ROB-11876 [part_number=ROB-11876]
  Barrel_Jack_for_12V_Power = Power Jack [package=power_jack_pth]
  RJ45_Keystone = RJ45 Jack [package=rj45-8]
  Dosing_Pump_B1 = Stepper Motor - Bipolar [part_number=" Kamoer KCS-Plus SM8B04"]
  Dosing_Pump_B2 = Stepper Motor - Bipolar [part_number=" Kamoer KCS-Plus SM8B04"]
  Dosing_Pump_A2 = Stepper Motor - Bipolar [part_number=" Kamoer KCS-Plus SM8B04"]  # not connected
  Dosing_Pump_A1 = Stepper Motor - Bipolar [part_number=" Kamoer KCS-Plus SM8B04"]  # not connected

nets:
  GND: Part3.GND, PART5.GND, PART6.GND, Part2.GND, PART3.GND, PART4.GND, Barrel_Jack_for_12V_Power.GND, RJ45_Keystone.5
  N1: Part3.VBAT, PART5.M+, PART6.M+, Part2.VBAT, PART3.M+, PART4.M+, Barrel_Jack_for_12V_Power.PWR
  VCC: Part3.+3V3, PART5.VCC, PART6.VCC, Part2.+3V3, PART3.VCC, PART4.VCC
  N2: Part3.D8, PART5.ENABLE
  N3: Part3.D6, PART5.M3
  N4: Part3.D5, PART5.M1
  N5: Part3.D4, PART5.MS2
  N6: Part3.D3, PART5.ST
  N7: Part3.D9, PART6.ST
  N8: Part3.D10, PART6.DR
  N9: Part3.D11, PART6.M1
  N10: Part3.D12, PART6.MS2
  N11: Part3.A0, PART5.DIR, PART5.DR
  N12: Part3.A1, PART6.M3
  N13: Part3.A2, PART6.ENABLE
  N14: Part3.A4, Part2.A4, RJ45_Keystone.6
  N15: Part3.A5, Part2.A5, RJ45_Keystone.2
  N16: PART5.B#2, Dosing_Pump_B1.C
  N17: PART5.B#3, Dosing_Pump_B1.A
  N18: PART5.A#17, Dosing_Pump_B1.D
  N19: PART5.A#18, Dosing_Pump_B1.B
  N20: Part2.D8, PART3.ENABLE
  N21: Part2.D6, PART3.M3
  N22: Part2.D5, PART3.M1
  N23: Part2.D4, PART3.MS2
  N24: Part2.D3, PART3.ST
  N25: Part2.D9, PART4.ST
  N26: Part2.D10, PART4.DR
  N27: Part2.D11, PART4.M1
  N28: Part2.D12, PART4.MS2
  N29: Part2.A0, PART3.DR
  N30: Part2.A1, PART4.M3
  N31: Part2.A2, PART4.ENABLE
  N32: PART3.B#2, Dosing_Pump_B2.C
  N33: PART3.B#3, Dosing_Pump_B2.A
  N34: PART3.A#17, Dosing_Pump_B2.D
  N35: PART3.A#18, Dosing_Pump_B2.B

custom parts:
  Adafruit Pro Trinket 3.3V 12MHz: rinket's got a big sister in town - the Pro Trinket 3V! Pro Trinket combines everything you love about Trinket with the familiarity of the core Arduino chip, the ATmega328. It's like an Arduino Pro Mini with more pins and USB tossed in. Trinket's a year old now, and while its been great to see tons of tiny projects, sometimes you just need more pins, more FLASH, and more RAM. That's why we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
  Big Easy Driver ROB-11876: The Big Easy Driver, designed by Brian Schmalz, is a stepper motor driver board for bi-polar stepper motors up to 1.4A/phase. It is based on the Allegro A4988 stepper driver chip. It’s the next version of the popular Easy Driver board. Each Big Easy Driver can drive up to about 1.4A per phase of a bi-polar stepper motor. It is a chopper microstepping driver which defaults to 16 step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
  Stepper Motor - Bipolar: Simple, but very powerful bi polar stepper motor. 4 wire
