# Fritzing sketch ReactionChamber (saved by Fritzing 0.9.3b)
breadboards: 1

parts:
  RJ45_Keystone = RJ45 Jack [package=rj45-8]
  Barrel_Jack_for_12V_power = Power Jack [package=power_jack_combo]
  part = Ailavi DC-DC 12V/24V To 5V 3A USB [part_number="Ailavi DC-DC 6V-24V to 5V 3A USB "]
  PART3 = Motor Driver 1A Dual TB6612FNG [part_number=ROB_09457]
  2600_RPM = DC Motor [part_number="Micro Gear Motor"]
  Isolation1 = Isolation Breakout
  MinipH2 = MinipH  # not connected
  Part1 = Adafruit TCS34725 RGB Color Sensor [part_number="Adafruit #1334"]
  W = Raspberry Pi Zero

nets:
  N1: RJ45_Keystone.2, Isolation1.SCL, Part1.SCL
  GND: RJ45_Keystone.5, part.OUT-, PART3.GND#8, Isolation1.GND, Part1.GND
  N2: RJ45_Keystone.6, Isolation1.SDA, Part1.SDA
  N3: Barrel_Jack_for_12V_power.GND, part.IN-, PART3.GND#7
  N4: Barrel_Jack_for_12V_power.PWR, part.IN+, PART3.VM
  VIN: PART3.VCC, Isolation1.VIN, Part1.VIN, W.3v3, W.3V3
  N5: PART3.A01, 2600_RPM.pin_1
  N6: PART3.A02, 2600_RPM.pin_2
  N7: Part1.LED_EN, W.GPIO23

notes:
  USB Cable

custom parts:
  Motor Driver 1A Dual TB6612FNG: The TB6612FNG motor driver can control up to two DC motors at a constant current of 1.2A (3.2A peak). Two input signals (IN1 and IN2) can be used to control the motor in one of four function modes - CW, CCW, short-brake, and stop. The two motor outputs (A and B) can be separately controlled, the speed of each motor is controlled via a PWM input signal with a frequency up to 100kHz. The STBY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
  Isolation Breakout: 24LC128 I2C EEPROM
  Adafruit TCS34725 RGB Color Sensor: Your electronics can now see in dazzling color with this lovely color light sensor. We found the best color sensor on the market, the TCS34725, which has RGB and Clear light sensing elements. An IR blocking filter, integrated on-chip and localized to the color sensing photodiodes, minimizes the IR spectral component of the incoming light and allows color measurements to be made accurately. The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
